// Logisim project lab4.circ as structural Verilog: 2 circuits, main circuit main2
module main (
  input  [1:0] A,
  input  [1:0] B,
  output L0,
  output L1,
  output L2
);

  wire and_1_out, and_2_out, and_3_out, and_4_out, and_5_out, and_6_out, and_7_out, and_8_out, not_1_out,
       not_2_out, not_3_out, not_4_out, not_5_out, not_6_out, not_7_out, not_8_out, not_9_out;

  not not_1 (not_1_out, B[0]);
  not not_2 (not_2_out, B[1]);
  and and_1 (and_1_out, not_2_out, not_1_out);
  and and_2 (and_2_out, A[1], A[0]);
  not not_3 (not_3_out, B[1]);
  and and_3 (and_3_out, A[0], not_3_out);
  and and_4 (and_4_out, A[1], not_5_out);
  or or_1 (L1, and_1_out, and_2_out, and_3_out, and_4_out, and_5_out);
  not not_4 (not_4_out, B[0]);
  not not_5 (not_5_out, B[1]);
  and and_5 (and_5_out, not_4_out, A[1]);
  not not_6 (not_6_out, B[1]);
  and and_6 (and_6_out, A[1], not_6_out);
  not not_7 (not_7_out, B[1]);
  not not_8 (not_8_out, B[0]);
  not not_9 (not_9_out, B[0]);
  and and_7 (and_7_out, A[0], not_7_out, not_8_out);
  or or_2 (L2, and_6_out, and_7_out, and_8_out);
  and and_8 (and_8_out, not_9_out, A[1], A[0]);

  assign L0 = 1'b1;
endmodule

module main2 (
  input  [1:0] A,
  input  [1:0] B
);

  wire _2Bit_Com_l0, _2Bit_Com_l1, _2Bit_Com_l2;

  main _2Bit_Com (.A(A), .B(B), .L0(_2Bit_Com_l0), .L1(_2Bit_Com_l1), .L2(_2Bit_Com_l2));
  LED L0 (.in(_2Bit_Com_l0));
  LED L2 (.in(_2Bit_Com_l2));
  LED L1 (.in(_2Bit_Com_l1));
endmodule
